# Fritzing sketch telecomande-base (saved by Fritzing 0.8.7b)
stripboards: 2

parts:
  Heltec_WiFi_LoRa_32_V1 = Heltec WiFi LoRa 32 V2 [part_number=HTIT-WB32LA]
  Part1 = Thumb Joystick  # not connected
  Part2 = Arduino Nano (Rev3.0)  # not connected
  S10 = Pushbutton [package="[THT]"]
  S11 = Pushbutton [package="[THT]"]  # not connected
  S19 = Pushbutton [package="[THT]"]
  S20 = Pushbutton [package="[THT]"]
  S21 = Pushbutton [package="[THT]"]
  S22 = Pushbutton [package="[THT]"]  # not connected
  S23 = Pushbutton [package="[THT]"]  # not connected
  S24 = Pushbutton [package="[THT]"]  # not connected
  S25 = Pushbutton [package="[THT]"]
  S26 = Pushbutton [package="[THT]"]
  S27 = Pushbutton [package="[THT]"]
  S28 = Pushbutton [package="[THT]"]  # not connected
  S29 = Pushbutton [package="[THT]"]
  S30 = Pushbutton [package="[THT]"]  # not connected
  S31 = Pushbutton [package="[THT]"]
  S32 = Pushbutton [package="[THT]"]
  S33 = Pushbutton [package="[THT]"]  # not connected
  S34 = Pushbutton [package="[THT]"]  # not connected
  S35 = Pushbutton [package="[THT]"]
  S36 = Pushbutton [package="[THT]"]
  S37 = Pushbutton [package="[THT]"]  # not connected
  S38 = Pushbutton [package="[THT]"]
  S39 = Pushbutton [package="[THT]"]  # not connected
  S40 = Pushbutton [package="[THT]"]  # not connected
  S41 = Pushbutton [package="[THT]"]  # not connected
  S42 = Pushbutton [package="[THT]"]
  Part3 = Breakout Board for Electret Microphone  # not connected
  Part4 = Triple Axis Accelerometer Breakout - ADXL345  # not connected
  Part5 = Color Sensor Breakout ADJD-S311  # not connected

nets (from the schematic view):
  N1: Heltec_WiFi_LoRa_32_V1.pin_16, Heltec_WiFi_LoRa_32_V1.pin_17
  N2: Heltec_WiFi_LoRa_32_V1.pin_18, Heltec_WiFi_LoRa_32_V1.pin_19
  N3: Heltec_WiFi_LoRa_32_V1.pin_21, Heltec_WiFi_LoRa_32_V1.pin_22
  N4: S10.Pin_1, S10.Pin_2
  N5: S10.Pin_3, S10.Pin_4
  N6: S19.Pin_1, S19.Pin_2
  N7: S19.Pin_3, S19.Pin_4
  N8: S20.Pin_1, S20.Pin_2
  N9: S20.Pin_3, S20.Pin_4
  N10: S21.Pin_1, S21.Pin_2
  N11: S21.Pin_3, S21.Pin_4
  N12: S25.Pin_1, S25.Pin_2
  N13: S26.Pin_1, S26.Pin_2
  N14: S26.Pin_3, S26.Pin_4
  N15: S27.Pin_1, S27.Pin_2
  N16: S27.Pin_3, S27.Pin_4
  N17: S29.Pin_1, S29.Pin_2
  N18: S29.Pin_3, S29.Pin_4
  N19: S31.Pin_1, S31.Pin_2
  N20: S31.Pin_3, S31.Pin_4
  N21: S32.Pin_1, S32.Pin_2
  N22: S35.Pin_1, S35.Pin_2
  N23: S35.Pin_3, S35.Pin_4
  N24: S36.Pin_1, S36.Pin_2
  N25: S36.Pin_3, S36.Pin_4
  N26: S38.Pin_1, S38.Pin_2
  N27: S42.Pin_1, S42.Pin_2
  N28: S42.Pin_3, S42.Pin_4

custom parts:
  Heltec WiFi LoRa 32 V2: Heltec WiFi LoRa 32 V2 WiFi LoRa 32 is a classic IoT dev-board designed & produced by Heltec Automation(TM). It’s a highly integrated product based on ESP32 + SX127x, it has Wi-Fi, BLE, LoRa functions, also Li-Po battery management system, 0.96″ OLED are also included. It’s the best choice for smart cities, smart farms, smart home, and IoT makers.
